// Logisim project ULA 4 BITS EP_02.circ as structural Verilog: 1 circuit, main circuit main
module main (
  input  [3:0] in_1,
  input  [3:0] ENTRADA_A,
  input  [3:0] ENTRADA_B,
  output [3:0] out_4
);

  wire [3:0] and_1_out, and_2_out, and_3_out, and_4_out, not_1_out, not_2_out, not_3_out, not_4_out,
       not_5_out, not_6_out, not_7_out, not_8_out, not_9_out, or_1_out, or_2_out, or_3_out, or_4_out,
       xor_1_out, xor_2_out;

  assign not_1_out = ~ENTRADA_B;  // NOT_Gate not_1, 4 bits wide
  assign or_1_out = ENTRADA_A | not_1_out;  // OR_Gate or_1, 4 bits wide
  assign or_2_out = ENTRADA_A | ENTRADA_B;  // OR_Gate or_2, 4 bits wide
  assign and_1_out = ENTRADA_A & ENTRADA_B;  // AND_Gate and_1, 4 bits wide
  assign not_2_out = ~ENTRADA_A;  // NOT_Gate not_2, 4 bits wide
  assign xor_1_out = ENTRADA_A ^ ENTRADA_B;  // XOR_Gate xor_1, 4 bits wide
  assign and_2_out = ENTRADA_A & not_4_out;  // AND_Gate and_2, 4 bits wide
  assign or_3_out = not_2_out | ENTRADA_B;  // OR_Gate or_3, 4 bits wide
  assign not_3_out = ~xor_1_out;  // NOT_Gate not_3, 4 bits wide
  assign not_4_out = ~ENTRADA_B;  // NOT_Gate not_4, 4 bits wide
  assign not_5_out = ~ENTRADA_B;  // NOT_Gate not_5, 4 bits wide
  assign xor_2_out = ENTRADA_A ^ ENTRADA_B;  // XOR_Gate xor_2, 4 bits wide
  assign not_6_out = ~ENTRADA_A;  // NOT_Gate not_6, 4 bits wide
  assign and_3_out = ENTRADA_A & ENTRADA_B;  // AND_Gate and_3, 4 bits wide
  assign and_4_out = not_6_out & ENTRADA_B;  // AND_Gate and_4, 4 bits wide
  assign not_7_out = ~and_3_out;  // NOT_Gate not_7, 4 bits wide
  assign or_4_out = ENTRADA_A | ENTRADA_B;  // OR_Gate or_4, 4 bits wide
  assign not_8_out = ~ENTRADA_A;  // NOT_Gate not_8, 4 bits wide
  assign not_9_out = ~or_4_out;  // NOT_Gate not_9, 4 bits wide
  Multiplexer #(.select(4), .width(4), .enable("false")) multiplexer_1 (
    .in0(not_8_out), .in1(not_9_out), .in2(and_4_out), .in3(4'b0000), .in4(not_7_out), .in5(not_5_out),
    .in6(xor_2_out), .in7(and_2_out), .in8(or_3_out), .in9(not_3_out), .in10(ENTRADA_B), .in11(and_1_out),
    .in12(4'b0001), .in13(or_1_out), .in14(or_2_out), .in15(ENTRADA_A), .out(out_4), .sel(in_1));
endmodule
